// Logisim project Pedra_papel_tesoura.circ as structural Verilog: 4 circuits, main circuit main
module main (
  input  in_1,
  input  in_2,
  input  in_3,
  input  in_4,
  input  in_5,
  input  in_6
);

  wire Jogador_1_x, Jogador_1_y, Jogador_2_x, Jogador_2_y, modulo2_1_x, modulo2_1_y, modulo3_1_x,
       modulo3_1_y, modulo3_1_z;

  Modulo1 Jogador_1 (.Pedra(in_1), .Papel(in_2), .Tesoura(in_3), .x(Jogador_1_x), .y(Jogador_1_y));
  Modulo1 Jogador_2 (.Pedra(in_4), .Papel(in_5), .Tesoura(in_6), .x(Jogador_2_x), .y(Jogador_2_y));
  Modulo2 modulo2_1 (
    .a(Jogador_1_x), .b(Jogador_1_y), .c(Jogador_2_x), .d(Jogador_2_y), .x(modulo2_1_x), .y(modulo2_1_y));
  Modulo3 modulo3_1 (.a(modulo2_1_x), .b(modulo2_1_y), .x(modulo3_1_x), .y(modulo3_1_y), .z(modulo3_1_z));
  LED Jogador1 (.in(modulo3_1_x));
  LED Empate (.in(modulo3_1_y));
  LED Jogador2 (.in(modulo3_1_z));

  // Notes on the sheet:
  //   x    y
  //   1   1 = Pedra
  //   1  0 = Papel
  //   0  1 = Tesoura
  //   0  0 = Inválido
  //   a   b
  //   1  1 = Empate
  //   0  1 = Jogador 1 vence
  //   1  0 = Jogador 2 vence
endmodule

module Modulo1 (
  input  Pedra,
  input  Papel,
  input  Tesoura,
  output x,
  output y
);

  wire and_1_out, and_2_out, and_3_out, and_4_out, not_1_out, not_2_out, not_3_out;

  not not_1 (not_1_out, Pedra);
  not not_2 (not_2_out, Papel);
  not not_3 (not_3_out, Tesoura);
  and and_1 (and_1_out, not_1_out, Papel, not_3_out);
  and and_2 (and_2_out, Pedra, not_2_out, not_3_out);
  and and_3 (and_3_out, not_1_out, not_2_out, Tesoura);
  and and_4 (and_4_out, Pedra, not_2_out, not_3_out);
  or or_1 (x, and_1_out, and_2_out);
  or or_2 (y, and_3_out, and_4_out);
endmodule

module Modulo2 (
  input  a,
  input  b,
  input  c,
  input  d,
  output x,
  output y
);

  wire and_1_out, and_2_out, and_3_out, and_4_out, and_5_out, and_6_out, and_7_out, and_8_out, not_1_out,
       not_2_out, not_3_out, not_4_out;

  not not_1 (not_1_out, a);
  not not_2 (not_2_out, b);
  not not_3 (not_3_out, c);
  not not_4 (not_4_out, d);
  and and_1 (and_1_out, not_1_out, b, d);
  and and_2 (and_2_out, a, not_2_out, not_3_out, d);
  and and_3 (and_3_out, a, c, not_4_out);
  and and_4 (and_4_out, b, c, d);
  and and_5 (and_5_out, b, not_3_out, d);
  and and_6 (and_6_out, not_1_out, b, c, not_4_out);
  and and_7 (and_7_out, a, not_2_out, c);
  and and_8 (and_8_out, a, c, d);
  or or_1 (x, and_1_out, and_2_out, and_3_out, and_4_out);
  or or_2 (y, and_5_out, and_6_out, and_7_out, and_8_out);
endmodule

module Modulo3 (
  input  a,
  input  b,
  output x,
  output y,
  output z
);

  wire not_1_out, not_2_out;

  not not_1 (not_1_out, a);
  not not_2 (not_2_out, b);
  and and_1 (x, not_1_out, b);
  and and_2 (y, a, b);
  and and_3 (z, a, not_2_out);
endmodule
